# Fritzing sketch Jarilo (saved by Fritzing 0.9.2b)
circuit board: 8.46667cm x 5.64444cm
breadboards: 1

parts:
  R5 = Resistor [tolerance=±5% resistance=10M package="0402 [SMD]"]
  R7 = Resistor [tolerance=±5% resistance=10M package="0402 [SMD]"]
  R8 = Resistor [tolerance=±5% resistance=10M package="0402 [SMD]"]
  R9 = Resistor [tolerance=±5% resistance=10M package="0402 [SMD]"]
  Part1 = Arduino Leonardo (Rev3b)
  R10 = Resistor [tolerance=±5% resistance=10M package="0402 [SMD]"]
  R11 = Resistor [tolerance=±5% resistance=10M package="0402 [SMD]"]

nets (from the breadboard view):
  N1: R5.Pin_0, R7.Pin_0, R8.Pin_0, R9.Pin_0, Part1.5V, R10.Pin_0, R11.Pin_0
  N2: R5.Pin_1, Part1.A3
  N3: R7.Pin_1, Part1.A0
  N4: R8.Pin_1, Part1.A1
  N5: R9.Pin_1, Part1.A2
  N6: Part1.A4, R10.Pin_1
  N7: Part1.A5, R11.Pin_1
